# Fritzing sketch 02-tlc-slider (saved by Fritzing 0.9.1b)
breadboards: 1

parts:
  Raspberry_Pi_B_rev1 = Raspberry Pi B rev1
  510R = Resistor [package="0402 [SMD]"]
  IC1 = IC, DIP package, 8 pins [chip_label=MCP3001]
  part = Rotary Potentiometer (Large) [maximum_resistance=100kΩ package=THT]

nets:
  N1: Raspberry_Pi_B_rev1.3V3, IC1.pin1, IC1.pin8, part.leg1
  N2: Raspberry_Pi_B_rev1.GND, 510R.Pin_0, IC1.pin3, IC1.pin4
  N3: Raspberry_Pi_B_rev1.GPIO_9, IC1.pin6
  N4: Raspberry_Pi_B_rev1.GPIO_11, IC1.pin7
  N5: Raspberry_Pi_B_rev1.GPIO_8, IC1.pin5
  N6: 510R.Pin_1, IC1.pin2, part.wiper
